# Fritzing sketch OpenKeyer - 16x2 LCD - Serial (saved by Fritzing 0.9.9b)
breadboards: 1

parts:
  Part1 = Arduino Nano (Rev3.0)
  LCD1 = LCD screen

nets:
  GND: Part1.GND, LCD1.VSS, LCD1.R/W
  N1: Part1.D8, LCD1.DB7
  N2: Part1.D9, LCD1.DB6
  N3: Part1.D10, LCD1.DB5
  N4: Part1.D11/MOSI, LCD1.DB4
  N5: Part1.D12/MISO, LCD1.E
  5V: Part1.5V, LCD1.VDD, LCD1.LED+
  N6: Part1.D13/SCK, LCD1.RS
