# Fritzing sketch OpenKeyer (saved by Fritzing 0.9.8b)
breadboards: 2

parts:
  Part1 = Arduino Nano (Rev3.0)
  LED1 = LED - 5mm [color="Red (633nm)" current=0.030 package="5 mm [THT]"]
  R1 = Resistor [tolerance=±5% power=0.25 resistance=220 package=THT]
  S1 = Pushbutton [package="[THT]"]
  S2 = Pushbutton [package="[THT]"]
  IC1 = IC, DIP package, 10 pins [chip_label=LM386]  # not connected
  SPKR1 = Loudspeaker  # not connected
  LCD1 = LCD screen
  S3 = Toggle Switch [package=THT]
  VCC1 = 4 x AAA Battery Mount
  TRS1 = Audio Jack (TRS) 3.5mm [package="4Ucon 08780 [THT]"]  # not connected
  RE2 = Rotary Encoder [package=THT]  # not connected
  S4 = Pushbutton [package="[THT]"]
  R2 = Rotary Potentiometer (Small) [maximum_resistance=100kΩ package=THT]  # not connected
  R3 = Rotary Potentiometer (Small) [maximum_resistance=100kΩ package=THT]  # not connected
  R4 = Trimmer Potentiometer [maximum_resistance=10kΩ package=THT]  # not connected
  J1 = female pin header, 2 pins [form="♀ (female)"]
  R5 = Resistor [tolerance=±5% power=0.25 resistance=220 package=THT]
  R6 = Resistor [tolerance=±5% power=0.25 resistance=220 package=THT]
  C1 = Electrolytic Capacitor [capacitance=1µF voltage=35V package="100 mil [THT, electrolytic]"]

nets:
  GND: Part1.GND, LCD1.VSS, LCD1.R/W, VCC1.-
  N1: Part1.D2, LCD1.DB7
  N2: Part1.D3, LCD1.DB6
  N3: Part1.D4, LCD1.DB5
  N4: Part1.D5, LCD1.DB4
  N5: Part1.D11/MOSI, LCD1.E
  N6: Part1.D12/MISO, LCD1.RS
  VIN: Part1.VIN, LCD1.VDD, S3.COM
  N7: LED1.cathode, R1.Pin_1
  N8: S1.Pin_1, S1.Pin_2
  N9: S1.Pin_3, S1.Pin_4
  N10: S2.Pin_1, S2.Pin_2
  N11: S2.Pin_3, S2.Pin_4
  N12: S3.L1, VCC1.+
  N13: S4.Pin_1, S4.Pin_2
  N14: S4.Pin_3, S4.Pin_4
  N15: J1.pin2, R5.Pin_0
  N16: R5.Pin_1, R6.Pin_0, C1.+
